# Fritzing sketch MiniProject(temperature display) (saved by Fritzing 1.0.1rc)
breadboards: 1

parts:
  LCD2 = LCD screen
  R4 = Trimmer Potentiometer [maximum_resistance=10kΩ knob_status=50% power=0.5W package=THT]
  R6 = Resistor [tolerance=±5% power=0.25W resistance=220 package=THT]
  LED1 = RGB LED (com. anode, rbg) [color="Red (633nm)" current=0.030A package="5 mm [THT]"]
  R7 = Resistor [tolerance=±5% power=0.25W resistance=330 package=THT]
  R8 = Resistor [tolerance=±5% power=0.25W resistance=330 package=THT]
  R9 = Resistor [tolerance=±5% power=0.25W resistance=330 package=THT]
  J1 = Piezo Speaker
  Part2 = Arduino Uno (Rev3)
  S1 = Pushbutton [package="[THT]"]
  R10 = Resistor [tolerance=±5% power=0.25W resistance=1k package=THT]
  DHT1 = DHT11 Humitidy and Temperature Sensor
  R11 = Resistor [tolerance=±5% power=0.25W resistance=4.7k package=THT]

nets (from the breadboard view):
  GND: LCD2.VSS, LCD2.R/W, LCD2.LED-, R4.leg1, J1.pin1, Part2.GND, R10.Pin_1, DHT1.GND
  VDD: LCD2.VDD, R4.leg2, R6.Pin_0, LED1.common_anode, Part2.5V, S1.Pin_1, S1.Pin_2, DHT1.VDD, R11.Pin_1
  N1: LCD2.V0, R4.wiper
  N2: LCD2.RS, Part2.D12/MISO
  N3: LCD2.DB4, Part2.D5_PWM
  N4: LCD2.DB5, Part2.D4
  N5: LCD2.DB6, Part2.D3_PWM
  N6: LCD2.DB7, Part2.D2
  N7: LCD2.LED+, R6.Pin_1
  N8: LED1.red_cathode, R7.Pin_1
  N9: LED1.blue_cathode, R8.Pin_1
  N10: LED1.green_cathode, R9.Pin_1
  N11: R7.Pin_0, Part2.D8
  N12: R8.Pin_0, Part2.D7
  N13: R9.Pin_0, Part2.D6_PWM
  N14: J1.pin2, Part2.D9_PWM
  N15: Part2.D13/SCK, DHT1.DATA, R11.Pin_0
  N16: S1.Pin_3, S1.Pin_4, R10.Pin_0

notes:
  Chan Antony (20179611) Temperature Displayer

custom parts:
  DHT11 Humitidy and Temperature Sensor: DHT11 Humidity and Temperature Sensor
